# Fritzing sketch pico_game_v2-1 (saved by Fritzing 1.0.2b)
circuit board: 10cm x 7.8cm
breadboards: 1

parts:
  Mod1 = Raspberry Pi Pico
  micro_SD1 = IC, SIP package, 6 pins [chip_label="micro SD"]
  A_BUTTON = Pushbutton [package="[THT]"]
  B_BUTTON = Pushbutton [package="[THT]"]
  UP_BUTTON = Pushbutton [package="[THT]"]
  DOWN_BUTTON = Pushbutton [package="[THT]"]
  LEFT_BUTTON = Pushbutton [package="[THT]"]
  RIGHT_BUTTON = Pushbutton [package="[THT]"]
  SELECT_BUTTON = Pushbutton [package="[THT]"]
  Adafruit_EYESPI1 = IC, DIP package, 18 pins [chip_label="Adafruit 5613"]

nets:
  N1: Mod1.pin_3, Mod1.pin_18, Mod1.pin_38, micro_SD1.pin1, A_BUTTON.Pin_1, A_BUTTON.Pin_2, B_BUTTON.Pin_1, B_BUTTON.Pin_2, UP_BUTTON.Pin_3, UP_BUTTON.Pin_4, DOWN_BUTTON.Pin_3, DOWN_BUTTON.Pin_4, LEFT_BUTTON.Pin_1, LEFT_BUTTON.Pin_2, RIGHT_BUTTON.Pin_3, RIGHT_BUTTON.Pin_4, SELECT_BUTTON.Pin_1, SELECT_BUTTON.Pin_2, Adafruit_EYESPI1.pin3
  N2: Mod1.pin_7, B_BUTTON.Pin_3, B_BUTTON.Pin_4
  N3: Mod1.pin_9, A_BUTTON.Pin_3, A_BUTTON.Pin_4
  N4: Mod1.pin_10, SELECT_BUTTON.Pin_3, SELECT_BUTTON.Pin_4
  N5: Mod1.pin_12, Adafruit_EYESPI1.pin9
  N6: Mod1.pin_14, Adafruit_EYESPI1.pin8
  N7: Mod1.pin_17, Adafruit_EYESPI1.pin7
  N8: Mod1.pin_19, Adafruit_EYESPI1.pin4
  N9: Mod1.pin_20, Adafruit_EYESPI1.pin5
  N10: Mod1.pin_21, micro_SD1.pin2
  N11: Mod1.pin_22, micro_SD1.pin5
  N12: Mod1.pin_24, micro_SD1.pin3
  N13: Mod1.pin_25, micro_SD1.pin4
  N14: Mod1.pin_29, LEFT_BUTTON.Pin_3, LEFT_BUTTON.Pin_4
  N15: Mod1.pin_31, UP_BUTTON.Pin_1, UP_BUTTON.Pin_2
  N16: Mod1.pin_32, RIGHT_BUTTON.Pin_1, RIGHT_BUTTON.Pin_2
  N17: Mod1.pin_34, DOWN_BUTTON.Pin_1, DOWN_BUTTON.Pin_2
  N18: Mod1.pin_36, micro_SD1.pin6, Adafruit_EYESPI1.pin1
  N19: Mod1.pin_39, Mod1.pin_40

notes:
  GP 0
  GND
  VSYS
  3v3
  PicoGame
  v 2 rev A

custom parts:
  Raspberry Pi Pico: Raspberry Pi Pico. Based around the RP2040 microcontroller the Pico is a low cost microcontroller device bringing Raspberry Pi quality, cost, and easy of use to the microcontroller space. Jan 2021, Split part in to two versions: tht (this one) and SMD. This one will drill holes for a .1 in header in pcb to allow plugging in the module as well as providing pads to solder the module to the top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
