# Fritzing sketch pico_game_v2 (saved by Fritzing 1.0.2b)
circuit board: 10cm x 7.76087cm
breadboards: 1

parts:
  Mod1 = Raspberry Pi Pico
  UP = Pushbutton [package="[THT]"]
  S2 = Toggle Switch [package=THT]
  DOWN = Pushbutton [package="[THT]"]
  LEFT = Pushbutton [package="[THT]"]
  RIGHT = Pushbutton [package="[THT]"]
  Adafruit_EYESPI = IC, DIP package, 18 pins [chip_label="Adafruit 5613"]
  A_BTN = Pushbutton [package="[THT]"]
  B_BTN = Pushbutton [package="[THT]"]
  SELECT = Pushbutton [package="[THT]"]
  micro_SD = IC, SIP package, 6 pins [chip_label="micro SD"]

nets (from the pcb view):
  N1: Mod1.pin_3, Mod1.pin_18, Mod1.pin_33, Mod1.pin_38, Mod1.pin_42, UP.Pin_1, UP.Pin_2, S2.L1, DOWN.Pin_1, DOWN.Pin_2, LEFT.Pin_1, LEFT.Pin_2, RIGHT.Pin_1, RIGHT.Pin_2, Adafruit_EYESPI.pin3, A_BTN.Pin_3, A_BTN.Pin_4, B_BTN.Pin_3, B_BTN.Pin_4, SELECT.Pin_3, SELECT.Pin_4, micro_SD.pin1
  N2: Mod1.pin_7, A_BTN.Pin_1, A_BTN.Pin_2
  N3: Mod1.pin_9, B_BTN.Pin_1, B_BTN.Pin_2
  N4: Mod1.pin_10, SELECT.Pin_1, SELECT.Pin_2
  N5: Mod1.pin_14, Adafruit_EYESPI.pin8
  N6: Mod1.pin_15, Adafruit_EYESPI.pin9
  N7: Mod1.pin_17, Adafruit_EYESPI.pin7
  N8: Mod1.pin_19, Adafruit_EYESPI.pin4
  N9: Mod1.pin_20, Adafruit_EYESPI.pin5
  N10: Mod1.pin_21, micro_SD.pin2
  N11: Mod1.pin_22, micro_SD.pin5
  N12: Mod1.pin_24, micro_SD.pin3
  N13: Mod1.pin_25, micro_SD.pin4
  N14: Mod1.pin_29, UP.Pin_3, UP.Pin_4
  N15: Mod1.pin_31, LEFT.Pin_3
  N16: Mod1.pin_32, RIGHT.Pin_3
  N17: Mod1.pin_34, DOWN.Pin_3, DOWN.Pin_4
  N18: Mod1.pin_36, Adafruit_EYESPI.pin1
  N19: Mod1.pin_37, micro_SD.pin6
  N20: Mod1.pin_39, S2.L2

notes:
  Gnd
  +
  PicoGame
  v 1 rev A
  Raspberry Pico

custom parts:
  Raspberry Pi Pico: Raspberry Pi Pico. Based around the RP2040 microcontroller the Pico is a low cost microcontroller device bringing Raspberry Pi quality, cost, and easy of use to the microcontroller space. Jan 2021, Split part in to two versions: tht (this one) and SMD. This one will drill holes for a .1 in header in pcb to allow plugging in the module as well as providing pads to solder the module to the top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
